// Logisim project Lab-11.circ as structural Verilog: 4 circuits, main circuit main
module main (
  input  D0,
  input  D1,
  input  C,
  input  D2,
  input  D3,
  input  in_6,
  input  in_7,
  input  in_8,
  input  in_9,
  input  in_10,
  input  in_11,
  input  in_12,
  input  in_13,
  input  [7:0] in_14,
  input  in_15,
  input  in_16,
  input  [3:0] in_17,
  input  L,
  input  [3:0] in_19,
  input  in_20,
  output Q0,
  output Q1,
  output Q2,
  output Q3,
  output [7:0] out_25,
  output Q0_2,
  output Q1_2,
  output Q2_2,
  output Q3_2,
  output [3:0] out_30,
  output _3,
  output _2,
  output _1,
  output _0,
  output _3_2,
  output _2_2,
  output _1_2,
  output _0_2
);

  wire and_1_out, button_2_out, button_3_out, button_4_out, button_5_out, button_out, C_out, clock_1_out,
       clock_2_out, clock_3_out, clock_4_out, clock_5_out, j_k_ff_1_qn, j_k_ff_2_qn, j_k_ff_3_qn,
       j_k_ff_4_qn, j_k_ff_5_qn, j_k_ff_6_qn, j_k_ff_7_qn, j_k_ff_8_qn, not_1_out, not_2_out, not_3_out,
       or_1_out, parallel_1_out_5, parallel_2_out_5, parallel_3_out_5, parallel_4_out_5;
  wire [3:0] calc_1_out_15, calc_1_out_16;

  Clock clock_1 (.out(clock_1_out));
  Clock clock_2 (.out(clock_2_out));
  not not_1 (not_1_out, L);
  Clock u_C (.out(C_out));
  Clock clock_3 (.out(clock_3_out));
  D_Flip_Flop d_ff_1 (.clk(clock_1_out), .D(D0), .Q(Q0));  // open: Qn, preset, en, reset
  D_Flip_Flop d_ff_2 (.clk(clock_1_out), .D(D1), .Q(Q1));  // open: Qn, preset, en, reset
  D_Flip_Flop d_ff_3 (.clk(clock_1_out), .D(D2), .Q(Q2));  // open: Qn, preset, en, reset
  D_Flip_Flop d_ff_4 (.clk(clock_1_out), .D(D3), .Q(Q3));  // open: Qn, preset, en, reset
  Clock clock_4 (.out(clock_4_out));
  Parallel parallel_1 (.Qin(out_30[0]), .nLoad(not_1_out), .D(in_19[0]), .Load(L), .out_5(parallel_1_out_5));
  Parallel parallel_2 (.Qin(out_30[1]), .nLoad(not_1_out), .D(in_19[1]), .Load(L), .out_5(parallel_2_out_5));
  Parallel parallel_3 (.Qin(out_30[2]), .nLoad(not_1_out), .D(in_19[2]), .Load(L), .out_5(parallel_3_out_5));
  Parallel parallel_4 (.Qin(out_30[3]), .nLoad(not_1_out), .D(in_19[3]), .Load(L), .out_5(parallel_4_out_5));
  Clock clock_5 (.out(clock_5_out));
  and and_1 (and_1_out, _1_2, _2_2, _3_2);
  not not_2 (not_2_out, and_1_out);
  Register register_1 (.D(in_14), .Q(out_25), .clk(clock_4_out), .clr(in_15));  // open: en
  not not_3 (not_3_out, in_16);
  D_Flip_Flop d_ff_5 (.clk(or_1_out), .D(in_17[0]), .Q(Q0_2));  // open: Qn, preset, en, reset
  D_Flip_Flop d_ff_6 (.clk(or_1_out), .D(in_17[1]), .Q(Q1_2));  // open: Qn, preset, en, reset
  D_Flip_Flop d_ff_7 (.clk(or_1_out), .D(in_17[2]), .Q(Q2_2));  // open: Qn, preset, en, reset
  D_Flip_Flop d_ff_8 (.clk(or_1_out), .D(in_17[3]), .Q(Q3_2));  // open: Qn, preset, en, reset
  D_Flip_Flop d_ff_9 (.clk(C_out), .D(parallel_1_out_5), .Q(out_30[0]));  // open: Qn, preset, en, reset
  D_Flip_Flop d_ff_10 (.clk(C_out), .D(parallel_2_out_5), .Q(out_30[1]));  // open: Qn, preset, en, reset
  D_Flip_Flop d_ff_11 (.clk(C_out), .D(parallel_3_out_5), .Q(out_30[2]));  // open: Qn, preset, en, reset
  D_Flip_Flop d_ff_12 (.clk(C_out), .D(parallel_4_out_5), .Q(out_30[3]));  // open: Qn, preset, en, reset
  J_K_Flip_Flop j_k_ff_1 (
    .J(in_20), .clk(clock_5_out), .K(j_k_ff_7_qn), .Q(_3), .Qn(j_k_ff_1_qn));  // open: preset, en, reset
  J_K_Flip_Flop j_k_ff_2 (
    .J(and_1_out), .clk(clock_3_out), .K(not_2_out), .Q(_3_2), .Qn(j_k_ff_2_qn));  // open: preset, en, reset
  or or_1 (or_1_out, clock_2_out, not_3_out);
  J_K_Flip_Flop j_k_ff_3 (
    .J(_3), .clk(clock_5_out), .K(j_k_ff_1_qn), .Q(_2), .Qn(j_k_ff_3_qn));  // open: preset, en, reset
  J_K_Flip_Flop j_k_ff_4 (
    .J(_3_2), .clk(clock_3_out), .K(j_k_ff_2_qn), .Q(_2_2), .Qn(j_k_ff_4_qn));  // open: preset, en, reset
  J_K_Flip_Flop j_k_ff_5 (
    .J(_2), .clk(clock_5_out), .K(j_k_ff_3_qn), .Q(_1), .Qn(j_k_ff_5_qn));  // open: preset, en, reset
  J_K_Flip_Flop j_k_ff_6 (
    .J(_2_2), .clk(clock_3_out), .K(j_k_ff_4_qn), .Q(_1_2), .Qn(j_k_ff_6_qn));  // open: preset, en, reset
  J_K_Flip_Flop j_k_ff_7 (
    .J(_1), .clk(clock_5_out), .K(j_k_ff_5_qn), .Q(in_20), .Qn(j_k_ff_7_qn));  // open: preset, en, reset
  J_K_Flip_Flop j_k_ff_8 (
    .J(_1_2), .clk(clock_3_out), .K(j_k_ff_6_qn), .Q(_0_2), .Qn(j_k_ff_8_qn));  // open: preset, en, reset
  Hex_Digit_Display hex_digit_display_1 (.value(calc_1_out_16));  // open: dp
  Hex_Digit_Display hex_digit_display_2 (.value(calc_1_out_15));  // open: dp
  Calc calc_1 (
    .in_1(in_6), .in_2(in_7), .in_3(in_8), .in_4(in_9), .in_5(in_10), .in_6(in_11), .in_7(in_12),
    .in_8(in_13), .in_10(button_2_out), .in_11(button_3_out), .in_12(button_4_out), .in_13(button_5_out),
    .in_14(button_out), .out_15(calc_1_out_15), .out_16(calc_1_out_16), .Clear(C));
  Button button (.out(button_out));
  Button button_2 (.out(button_2_out));
  Button button_3 (.out(button_3_out));
  Button button_4 (.out(button_4_out));
  Button button_5 (.out(button_5_out));

  assign _0 = in_20;
endmodule

module Parallel (
  input  Qin,
  input  nLoad,
  input  D,
  input  Load,
  output out_5
);

  wire and_1_out, and_2_out;

  and and_1 (and_1_out, Qin, nLoad);
  and and_2 (and_2_out, D, Load);
  or or_1 (out_5, and_1_out, and_2_out);
endmodule

module R_L (
  input  L,
  input  nR,
  input  L_2,
  input  R,
  output out_5
);

  wire and_1_out, and_2_out;

  and and_1 (and_1_out, L, nR);
  or or_1 (out_5, and_1_out, and_2_out);
  and and_2 (and_2_out, L_2, R);
endmodule

module Calc (
  input  in_1,
  input  in_2,
  input  in_3,
  input  in_4,
  input  in_5,
  input  in_6,
  input  in_7,
  input  in_8,
  input  Clear,
  input  in_10,
  input  in_11,
  input  in_12,
  input  in_13,
  input  in_14,
  output [3:0] out_15,
  output [3:0] out_16
);

  wire and_1_out, and_2_out, and_3_out, and_4_out, clock_1_out, d_ff_1_q, d_ff_2_q, d_ff_3_q, d_ff_4_q,
       d_ff_5_q, not_1_out, not_2_out, or_1_out;
  wire [7:0] adder_1_out, divider_1_out, multiplier_1_out, register_1_q, register_2_q, subtractor_1_out;

  not not_1 (not_1_out, or_1_out);
  Clock clock_1 (.out(clock_1_out));
  D_Flip_Flop d_ff_1 (.clk(in_14), .D(in_14), .Q(d_ff_1_q), .reset(Clear));  // open: Qn, preset, en
  Register register_1 (
    .D({in_8, in_7, in_6, in_5, in_4, in_3, in_2, in_1}), .en(not_1_out), .Q(register_1_q),
    .clk(clock_1_out), .clr(Clear));
  Register register_2 (
    .D({in_8, in_7, in_6, in_5, in_4, in_3, in_2, in_1}), .en(or_1_out), .Q(register_2_q), .clk(clock_1_out),
    .clr(Clear));
  Divider divider_1 (.a(register_1_q), .b(register_2_q), .out(divider_1_out));  // open: upper, rem
  Multiplier multiplier_1 (.a(register_1_q), .b(register_2_q), .out(multiplier_1_out));  // open: cin, cout
  Subtractor subtractor_1 (.a(register_1_q), .b(register_2_q), .out(subtractor_1_out));  // open: bin, bout
  Adder adder_1 (.a(register_1_q), .b(register_2_q), .out(adder_1_out));  // open: cin, cout
  assign out_15 = not_2_out ? {in_4, in_3, in_2, in_1} : 4'bz;  // Controlled_Buffer controlled_buffer_1
  assign out_16 = not_2_out ? {in_8, in_7, in_6, in_5} : 4'bz;  // Controlled_Buffer controlled_buffer_2
  assign out_15 = and_1_out ? divider_1_out[3:0] : 4'bz;  // Controlled_Buffer controlled_buffer_3
  assign out_16 = and_1_out ? divider_1_out[7:4] : 4'bz;  // Controlled_Buffer controlled_buffer_4
  assign out_15 = and_2_out ? multiplier_1_out[3:0] : 4'bz;  // Controlled_Buffer controlled_buffer_5
  assign out_16 = and_2_out ? multiplier_1_out[7:4] : 4'bz;  // Controlled_Buffer controlled_buffer_6
  assign out_15 = and_3_out ? subtractor_1_out[3:0] : 4'bz;  // Controlled_Buffer controlled_buffer_7
  assign out_16 = and_3_out ? subtractor_1_out[7:4] : 4'bz;  // Controlled_Buffer controlled_buffer_8
  assign out_15 = and_4_out ? adder_1_out[3:0] : 4'bz;  // Controlled_Buffer controlled_buffer_9
  assign out_16 = and_4_out ? adder_1_out[7:4] : 4'bz;  // Controlled_Buffer controlled_buffer_10
  D_Flip_Flop d_ff_2 (.clk(in_10), .D(in_10), .Q(d_ff_2_q), .reset(Clear));  // open: Qn, preset, en
  D_Flip_Flop d_ff_3 (.clk(in_11), .D(in_11), .Q(d_ff_3_q), .reset(Clear));  // open: Qn, preset, en
  D_Flip_Flop d_ff_4 (.clk(in_12), .D(in_12), .Q(d_ff_4_q), .reset(Clear));  // open: Qn, preset, en
  D_Flip_Flop d_ff_5 (.clk(in_13), .D(in_13), .Q(d_ff_5_q), .reset(Clear));  // open: Qn, preset, en
  not not_2 (not_2_out, d_ff_1_q);
  or or_1 (or_1_out, d_ff_2_q, d_ff_3_q, d_ff_4_q, d_ff_5_q);
  and and_1 (and_1_out, d_ff_1_q, d_ff_2_q);
  and and_2 (and_2_out, d_ff_1_q, d_ff_3_q);
  and and_3 (and_3_out, d_ff_1_q, d_ff_4_q);
  and and_4 (and_4_out, d_ff_1_q, d_ff_5_q);
endmodule
