// Logisim project Lab-8.circ as structural Verilog: 1 circuit, main circuit main
module main (
  input  A,
  input  B,
  input  C,
  input  [2:0] Ex__1,
  input  D,
  input  [2:0] Ex__2,
  input  [3:0] Ex__3,
  input  [1:0] Ex__4,
  input  Ex__5,
  input  [2:0] in_10,
  input  Ex_6,
  input  [1:0] in_12,
  input  [1:0] in_13,
  input  B0,
  input  CIN,
  input  A0,
  input  A0_2,
  input  B0_2,
  input  CIN_2,
  input  a0_3,
  input  a1,
  input  a2,
  input  a3,
  input  A0_4,
  input  B0_3,
  input  B1,
  input  A1_2,
  input  A1_3,
  input  B1_2,
  input  CIN_3,
  input  B2,
  input  A2_2,
  input  B3,
  input  A3_2,
  input  a0_5,
  input  a1_4,
  input  a2_3,
  input  a3_3,
  input  C_2,
  input  b0_4,
  input  b1_3,
  input  b2_2,
  input  b3_2,
  output F1,
  output F2,
  output F3,
  output F1_2,
  output x4,
  output x3,
  output x2,
  output x1,
  output x0,
  output F2_2,
  output F3_2,
  output F,
  output Sum,
  output b0_5,
  output Sum_0,
  output C_3,
  output b1_4,
  output Sum_4,
  output Sum_5,
  output b2_3,
  output C_4,
  output b3_3,
  output Sum_1,
  output Sum_2,
  output Sum_3,
  output COUT,
  output Carry,
  output Sum_0_2,
  output Sum_1_2,
  output Sum_2_2,
  output Sum_3_2
);

  wire and_1_out, and_2_out, and_3_out, and_4_out, and_5_out, and_6_out, and_7_out, and_8_out, and_9_out,
       and_10_out, and_11_out, and_12_out, and_13_out, and_14_out, and_15_out, and_16_out, and_17_out,
       and_18_out, and_19_out, and_20_out, and_21_out, and_22_out, and_23_out, and_24_out, and_25_out,
       and_26_out, and_27_out, and_28_out, and_29_out, and_30_out, and_31_out, and_32_out, and_33_out,
       and_34_out, and_35_out, and_36_out, and_37_out, and_38_out, and_39_out, and_40_out, and_41_out,
       and_42_out, and_43_out, decoder_1_out0, decoder_1_out1, decoder_1_out2, decoder_1_out3,
       decoder_1_out5, decoder_1_out7, decoder_2_out0, decoder_2_out1, decoder_2_out2, decoder_2_out3,
       decoder_2_out4, decoder_2_out5, decoder_2_out6, decoder_2_out7, decoder_3_out1, decoder_3_out3,
       decoder_3_out4, decoder_3_out9, decoder_3_out11, decoder_3_out12, decoder_3_out13, decoder_3_out14,
       decoder_3_out15, decoder_4_out0, decoder_4_out1, decoder_4_out2, decoder_4_out3, decoder_7_out0,
       decoder_7_out1, decoder_7_out2, decoder_7_out3, nand_1_out, nand_2_out, nand_3_out, nand_4_out,
       nand_5_out, nand_6_out, nand_7_out, nand_8_out, nand_9_out, nand_10_out, nand_11_out, nand_12_out,
       nand_13_out, nand_14_out, nand_15_out, nand_16_out, nand_17_out, nand_18_out, nand_19_out,
       nand_20_out, nand_21_out, nand_22_out, nand_23_out, nand_24_out, nand_25_out, nand_26_out,
       nand_27_out, nand_28_out, nand_29_out, nand_30_out, nand_31_out, nand_32_out, nand_33_out,
       nand_34_out, nand_35_out, nand_36_out, nand_37_out, nand_38_out, not_1_out, not_2_out, not_3_out,
       not_4_out, not_5_out, not_7_out, not_8_out, not_9_out, not_10_out, not_11_out, not_12_out, not_13_out,
       not_14_out, not_15_out, not_16_out, not_17_out, not_18_out, not_19_out, not_20_out, or_8_out,
       or_9_out, or_13_out, or_14_out, or_15_out, or_16_out, or_19_out, or_21_out, or_22_out, or_23_out,
       or_24_out, or_25_out, or_26_out, xor_1_out, xor_2_out, xor_3_out, xor_4_out, xor_5_out, xor_6_out,
       xor_7_out, xor_8_out, xor_12_out, xor_13_out, xor_14_out, xor_19_out, xor_20_out, xor_21_out,
       xor_22_out, xor_23_out, xor_24_out, xor_25_out, xor_26_out;

  not not_1 (not_1_out, Ex_6);
  not not_2 (not_2_out, a0_3);
  Decoder #(.select(3), .enable("false")) decoder_1 (
    .out0(decoder_1_out0), .out1(decoder_1_out1), .out2(decoder_1_out2), .out3(decoder_1_out3),
    .out5(decoder_1_out5), .out7(decoder_1_out7), .sel(Ex__1));  // open: out4, out6
  Decoder #(.select(3), .enable("false")) decoder_2 (
    .out0(decoder_2_out0), .out1(decoder_2_out1), .out2(decoder_2_out2), .out3(decoder_2_out3),
    .out4(decoder_2_out4), .out5(decoder_2_out5), .out6(decoder_2_out6), .out7(decoder_2_out7), .sel(Ex__2));
  Decoder #(.select(4), .enable("false")) decoder_3 (
    .out1(decoder_3_out1), .out3(decoder_3_out3), .out4(decoder_3_out4), .out9(decoder_3_out9),
    .out11(decoder_3_out11), .out12(decoder_3_out12), .out13(decoder_3_out13), .out14(decoder_3_out14),
    .out15(decoder_3_out15), .sel(Ex__3));  // open: out0, out2, out5, out6, out7, out8, out10
  Decoder #(.select(2), .enable("false")) decoder_4 (
    .out0(decoder_4_out0), .out1(decoder_4_out1), .out2(decoder_4_out2), .out3(decoder_4_out3), .sel(Ex__4));
  Decoder #(.select(3)) decoder_5 (
    .sel(in_10), .en(not_3_out));  // open: out0, out1, out2, out3, out4, out5, out6, out7
  not not_3 (not_3_out, Ex__5);
  Decoder #(.select(3)) decoder_6 (.sel(in_10), .en(Ex__5));  // open: out0, out1, out2, out3, out4, out5, out6, out7
  Decoder #(.select(2)) decoder_7 (
    .out0(decoder_7_out0), .out1(decoder_7_out1), .out2(decoder_7_out2), .out3(decoder_7_out3), .sel(in_12),
    .en(not_1_out));
  not not_4 (not_4_out, a1);
  not not_5 (not_5_out, a2);
  Decoder #(.select(2)) decoder_8 (.sel(in_13), .en(decoder_7_out0));  // open: out0, out1, out2, out3
  Decoder #(.select(2)) decoder_9 (.sel(in_13), .en(decoder_7_out1));  // open: out0, out1, out2, out3
  Decoder #(.select(2)) decoder_10 (.sel(in_13), .en(decoder_7_out2));  // open: out0, out1, out2, out3
  Decoder #(.select(2)) decoder_11 (.sel(in_13), .en(decoder_7_out3));  // open: out0, out1, out2, out3
  not not_6 (b3_3, a3);
  and and_1 (and_1_out, a0_5, a2_3, a3_3);
  and and_2 (and_2_out, a0_5, a1_4);
  not not_7 (not_7_out, a1_4);
  not not_8 (not_8_out, a2_3);
  not not_9 (not_9_out, a1_4);
  not not_10 (not_10_out, a3_3);
  not not_11 (not_11_out, a2_3);
  not not_12 (not_12_out, a3_3);
  not not_13 (not_13_out, a3_3);
  and and_3 (and_3_out, b0_4, b2_2, b3_2);
  and and_4 (and_4_out, b0_4, b1_3);
  not not_14 (not_14_out, b1_3);
  not not_15 (not_15_out, b2_2);
  not not_16 (not_16_out, b1_3);
  not not_17 (not_17_out, b3_2);
  not not_18 (not_18_out, b2_2);
  not not_19 (not_19_out, b3_2);
  not not_20 (not_20_out, b3_2);
  or or_1 (F1, decoder_1_out0, decoder_1_out2, decoder_1_out7);
  or or_2 (F2, decoder_1_out0, decoder_1_out2, decoder_1_out3);
  or or_3 (F3, decoder_1_out0, decoder_1_out1, decoder_1_out5);
  or or_4 (F1_2, decoder_2_out0, decoder_2_out3, decoder_2_out4);
  or or_5 (F2_2, decoder_2_out1, decoder_2_out2, decoder_2_out7);
  or or_6 (F3_2, decoder_2_out3, decoder_2_out5, decoder_2_out6, decoder_2_out7);
  or or_7 (F, decoder_3_out1, decoder_3_out3, decoder_3_out4, decoder_3_out9, decoder_3_out11, decoder_3_out12, decoder_3_out13, decoder_3_out14, decoder_3_out15);
  and and_5 (and_5_out, a0_3, a2, a3);
  and and_6 (and_6_out, a0_3, a1);
  and and_7 (and_7_out, not_4_out, not_5_out);
  and and_8 (and_8_out, not_4_out, b3_3);
  and and_9 (and_9_out, a1, a2, a3);
  and and_10 (and_10_out, not_5_out, a3);
  and and_11 (and_11_out, a2, b3_3);
  or or_8 (or_8_out, and_1_out, and_2_out);
  and and_12 (and_12_out, not_7_out, not_8_out);
  and and_13 (and_13_out, not_9_out, not_10_out);
  and and_14 (and_14_out, a1_4, a2_3, a3_3);
  and and_15 (and_15_out, not_11_out, a3_3);
  and and_16 (and_16_out, a2_3, not_12_out);
  or or_9 (or_9_out, and_3_out, and_4_out);
  and and_17 (and_17_out, not_14_out, not_15_out);
  and and_18 (and_18_out, not_16_out, not_17_out);
  and and_19 (and_19_out, b1_3, b2_2, b3_2);
  and and_20 (and_20_out, not_18_out, b3_2);
  and and_21 (and_21_out, b2_2, not_19_out);
  or or_10 (b0_5, and_5_out, and_6_out);
  or or_11 (b1_4, and_7_out, and_8_out, and_9_out);
  or or_12 (b2_3, and_10_out, and_11_out);
  or or_13 (or_13_out, and_12_out, and_13_out, and_14_out);
  or or_14 (or_14_out, and_15_out, and_16_out);
  or or_15 (or_15_out, and_17_out, and_18_out, and_19_out);
  or or_16 (or_16_out, and_20_out, and_21_out);
  xor xor_1 (xor_1_out, not_13_out, not_20_out);
  xor xor_2 (xor_2_out, B0_2, A0_2);
  and and_22 (and_22_out, B0_2, A0_2);
  xor xor_3 (xor_3_out, B0_3, A0_4);
  and and_23 (and_23_out, B0_3, A0_4);
  xor xor_4 (xor_4_out, B1_2, A1_3);
  and and_24 (and_24_out, B1_2, A1_3);
  xor xor_5 (xor_5_out, or_8_out, or_9_out);
  xor xor_6 (xor_6_out, or_13_out, or_15_out);
  xor xor_7 (xor_7_out, or_14_out, or_16_out);
  xor xor_8 (xor_8_out, xor_1_out, not_13_out);
  xor xor_9 (Sum, xor_2_out, CIN_2);
  and and_25 (and_25_out, xor_2_out, CIN_2);
  xor xor_10 (Sum_4, or_19_out, xor_3_out);
  and and_26 (and_26_out, or_19_out, xor_3_out);
  xor xor_11 (Sum_5, xor_4_out, CIN_3);
  and and_27 (and_27_out, xor_4_out, CIN_3);
  xor xor_12 (xor_12_out, xor_5_out, or_8_out);
  and and_28 (and_28_out, or_9_out, or_8_out);
  xor xor_13 (xor_13_out, xor_6_out, or_13_out);
  and and_29 (and_29_out, or_15_out, or_13_out);
  xor xor_14 (xor_14_out, xor_7_out, or_14_out);
  and and_30 (and_30_out, or_16_out, or_14_out);
  and and_31 (and_31_out, not_20_out, not_13_out);
  or or_17 (C_3, and_25_out, and_22_out);
  or or_18 (C_4, and_26_out, and_23_out);
  or or_19 (or_19_out, and_27_out, and_24_out);
  xor xor_15 (Sum_0_2, or_21_out, xor_12_out);
  and and_32 (and_32_out, or_21_out, xor_12_out);
  xor xor_16 (Sum_1_2, or_22_out, xor_13_out);
  and and_33 (and_33_out, or_22_out, xor_13_out);
  xor xor_17 (Sum_2_2, or_23_out, xor_14_out);
  and and_34 (and_34_out, or_23_out, xor_14_out);
  xor xor_18 (Sum_3_2, xor_8_out, C_2);
  and and_35 (and_35_out, xor_8_out, C_2);
  nand nand_1 (nand_1_out, A, A);
  nand nand_2 (nand_2_out, B, B);
  nand nand_3 (nand_3_out, C, C);
  nand nand_4 (nand_4_out, A, A);
  nand nand_5 (nand_5_out, B, B);
  nand nand_6 (nand_6_out, A, A);
  nand nand_7 (nand_7_out, C, C);
  nand nand_8 (nand_8_out, D, D);
  nand nand_9 (nand_9_out, B, B);
  nand nand_10 (nand_10_out, D, D);
  nand nand_11 (nand_11_out, A, A);
  nand nand_12 (nand_12_out, C, C);
  nand nand_13 (nand_13_out, D, D);
  nand nand_14 (nand_14_out, C, C);
  nand nand_15 (nand_15_out, D, D);
  nand nand_16 (nand_16_out, B, B);
  nand nand_17 (nand_17_out, C, C);
  nand nand_18 (nand_18_out, D, D);
  or or_20 (Carry, and_32_out, and_28_out);
  or or_21 (or_21_out, and_33_out, and_29_out);
  or or_22 (or_22_out, and_34_out, and_30_out);
  or or_23 (or_23_out, and_35_out, and_31_out);
  nand nand_19 (nand_19_out, B, B);
  nand nand_20 (nand_20_out, D, D);
  nand nand_21 (nand_21_out, C, C);
  nand nand_22 (nand_22_out, D, D);
  nand nand_23 (nand_23_out, nand_4_out, nand_5_out, D);
  nand nand_24 (nand_24_out, nand_6_out, nand_7_out, D);
  nand nand_25 (nand_25_out, A, nand_8_out);
  nand nand_26 (nand_26_out, nand_9_out, C);
  nand nand_27 (nand_27_out, C, nand_10_out);
  nand nand_28 (nand_28_out, A, D);
  nand nand_29 (nand_29_out, nand_11_out, nand_12_out, nand_13_out);
  nand nand_30 (nand_30_out, B, nand_14_out);
  nand nand_31 (nand_31_out, B, nand_15_out);
  nand nand_32 (nand_32_out, nand_16_out, nand_17_out, nand_18_out);
  nand nand_33 (nand_33_out, B, C, D);
  nand nand_34 (nand_34_out, A, A);
  nand nand_35 (nand_35_out, nand_1_out, nand_2_out, nand_3_out, D);
  nand nand_36 (nand_36_out, nand_19_out, C, nand_20_out);
  nand nand_37 (nand_37_out, B, nand_21_out, nand_22_out);
  nand nand_38 (nand_38_out, B, C, D);
  nand nand_39 (x3, nand_23_out, nand_24_out, nand_25_out);
  nand nand_40 (x2, nand_26_out, nand_27_out, nand_28_out);
  nand nand_41 (x1, nand_29_out, nand_30_out, nand_31_out);
  nand nand_42 (x0, nand_32_out, nand_33_out, nand_34_out);
  xor xor_19 (xor_19_out, B3, CIN);
  nand nand_43 (x4, nand_35_out, nand_36_out, nand_37_out, nand_38_out);
  xor xor_20 (xor_20_out, B0, CIN);
  xor xor_21 (xor_21_out, B1, CIN);
  xor xor_22 (xor_22_out, B2, CIN);
  xor xor_23 (xor_23_out, xor_20_out, A0);
  and and_36 (and_36_out, xor_20_out, A0);
  xor xor_24 (xor_24_out, xor_21_out, A1_2);
  and and_37 (and_37_out, xor_21_out, A1_2);
  xor xor_25 (xor_25_out, xor_22_out, A2_2);
  and and_38 (and_38_out, xor_22_out, A2_2);
  xor xor_26 (xor_26_out, xor_19_out, A3_2);
  and and_39 (and_39_out, xor_19_out, A3_2);
  xor xor_27 (Sum_0, xor_23_out, CIN);
  and and_40 (and_40_out, xor_23_out, CIN);
  xor xor_28 (Sum_1, xor_24_out, or_24_out);
  and and_41 (and_41_out, xor_24_out, or_24_out);
  xor xor_29 (Sum_2, xor_25_out, or_25_out);
  and and_42 (and_42_out, xor_25_out, or_25_out);
  xor xor_30 (Sum_3, xor_26_out, or_26_out);
  and and_43 (and_43_out, xor_26_out, or_26_out);
  or or_24 (or_24_out, and_40_out, and_36_out);
  or or_25 (or_25_out, and_41_out, and_37_out);
  or or_26 (or_26_out, and_42_out, and_38_out);
  or or_27 (COUT, and_43_out, and_39_out);

  // Notes on the sheet:
  //   Ex) 8 P 1
  //   Ex) 8 P 5
  //   Not Complete
  //   Ex) 8 P 2
  //   Ex) 8 P3
  //   Ex) 8 P4
  //   Ex) 7
  //   Ex) 8 P4
endmodule
